# Fritzing sketch ControlReceiverAndPropulsionSystem (saved by Fritzing 0.9.1b)
breadboards: 1

parts:
  Arduino = Arduino Uno (Rev3)
  RearWheelMotor = DC Motor  # not connected
  FrontWheelMotor = DC Motor  # not connected
  MotorBattery1 = Battery Holders [package=battery-aa]
  MotorBattery2 = Battery Holders [package=battery-aa]
  MotorBattery3 = Battery Holders [package=battery-aa]
  ForwardLED = smd LED [color="Red (660nm)" package="0603 [SMD]"]
  LeftLED = smd LED [color="Yellow (574nm)" package="0603 [SMD]"]
  RightLED = smd LED [color="Green (570nm)" package="0603 [SMD]"]
  U5 = BATTERY-2 [package=battery-aa]
  U6 = BATTERY-2 [package=battery-aa]
  U7 = BATTERY-2 [package=battery-aa]
  U8 = BATTERY-2 [package=battery-aa]
  VCC1 = Battery block 9V  # not connected

nets:
  N1: Arduino.D8, ForwardLED.anode
  N2: Arduino.D10_PWM/SS, Arduino.GND, ForwardLED.cathode, LeftLED.cathode, LeftLED.anode, RightLED.cathode, U8.+1
  N3: Arduino.D11_PWM/MOSI, RightLED.anode
  N4: MotorBattery1.+, MotorBattery2.-
  N5: MotorBattery2.+, MotorBattery3.-
  N6: MotorBattery3.+, U5.-1
  N7: U6.+1, U7.-1
  N8: U7.+1, U8.-1

notes:
  3.6V Rechargable
  600mAh
  6V
  ??mAh
  Front Motor
  Rear Motor
  Turn Left LED
  Turn Right LED
  Go Fiorward LED
